// Logisim project 7sigment.circ as structural Verilog: 8 circuits, main circuit hex_0
module main (
  input  c0,
  input  c1,
  input  c2,
  input  c3
);

  wire hex_0_1_hex0, hex_1_1_hex1, hex_2_1_hex2, hex_3_1_hex3, hex_4_1_hex4, hex_5_1_hex5, hex_6_1_hex6;

  hex_0 hex_0_1 (.c0(c0), .c1(c1), .c2(c2), .c3(c3), .hex0(hex_0_1_hex0));
  hex_1 hex_1_1 (.c0(c0), .c1(c1), .c2(c2), .c3(c3), .hex1(hex_1_1_hex1));
  hex_2 hex_2_1 (.c0(c0), .c1(c1), .c2(c2), .c3(c3), .hex2(hex_2_1_hex2));
  hex_3 hex_3_1 (.c0(c0), .c1(c1), .c2(c2), .c3(c3), .hex3(hex_3_1_hex3));
  hex_4 hex_4_1 (.c0(c0), .c1(c1), .c2(c2), .c3(c3), .hex4(hex_4_1_hex4));
  hex_5 hex_5_1 (.c0(c0), .c1(c1), .c2(c2), .c3(c3), .hex5(hex_5_1_hex5));
  hex_6 hex_6_1 (.c0(c0), .c1(c1), .c2(c2), .c3(c3), .hex6(hex_6_1_hex6));
  _7_Segment_Display L_7_Segment_Display_1 (
    .g(hex_6_1_hex6), .f(hex_5_1_hex5), .a(hex_0_1_hex0), .b(hex_1_1_hex1), .e(hex_4_1_hex4),
    .d(hex_3_1_hex3), .c(hex_2_1_hex2));  // open: dp
endmodule

module hex_0 (
  input  c0,
  input  c1,
  input  c2,
  input  c3,
  output hex0
);

  wire and_1_out, and_2_out, and_3_out, and_4_out, and_5_out, and_6_out, not_1_out, not_2_out, not_3_out,
       not_4_out;

  not not_1 (not_1_out, c0);
  not not_2 (not_2_out, c1);
  not not_3 (not_3_out, c2);
  not not_4 (not_4_out, c3);
  and and_1 (and_1_out, not_1_out, not_3_out);
  and and_2 (and_2_out, c1, not_4_out);
  and and_3 (and_3_out, not_4_out, c2, c0);
  and and_4 (and_4_out, c2, c1);
  and and_5 (and_5_out, c3, not_1_out);
  and and_6 (and_6_out, c3, not_2_out, not_3_out);
  or or_1 (hex0, and_1_out, and_2_out, and_3_out, and_4_out, and_5_out, and_6_out);

  // Notes on the sheet:
  //   HEX[0]
endmodule

module hex_1 (
  input  c0,
  input  c1,
  input  c2,
  input  c3,
  output hex1
);

  wire and_1_out, and_2_out, and_3_out, and_4_out, and_5_out, not_1_out, not_2_out, not_3_out, not_4_out;

  not not_1 (not_1_out, c0);
  not not_2 (not_2_out, c1);
  not not_3 (not_3_out, c2);
  not not_4 (not_4_out, c3);
  and and_1 (and_1_out, not_3_out, not_4_out);
  and and_2 (and_2_out, not_1_out, not_3_out);
  and and_3 (and_3_out, not_1_out, not_2_out, not_4_out);
  and and_4 (and_4_out, c0, not_2_out, c3);
  and and_5 (and_5_out, c0, c1, not_4_out);
  or or_1 (hex1, and_1_out, and_2_out, and_3_out, and_4_out, and_5_out);

  // Notes on the sheet:
  //   HEX[1]
endmodule

module hex_2 (
  input  c0,
  input  c1,
  input  c2,
  input  c3,
  output hex2
);

  wire and_1_out, and_2_out, and_3_out, and_4_out, and_5_out, not_1_out, not_2_out, not_3_out;

  not not_1 (not_1_out, c1);
  not not_2 (not_2_out, c2);
  not not_3 (not_3_out, c3);
  and and_1 (and_1_out, not_1_out, not_3_out);
  and and_2 (and_2_out, c0, not_3_out);
  and and_3 (and_3_out, not_1_out, c0);
  and and_4 (and_4_out, c2, not_3_out);
  and and_5 (and_5_out, not_2_out, c3);
  or or_1 (hex2, and_1_out, and_2_out, and_3_out, and_4_out, and_5_out);

  // Notes on the sheet:
  //   HEX[2]
endmodule

module hex_3 (
  input  c0,
  input  c1,
  input  c2,
  input  c3,
  output hex3
);

  wire and_1_out, and_2_out, and_3_out, and_4_out, and_5_out, not_1_out, not_2_out, not_3_out, not_4_out,
       not_5_out, not_6_out, not_7_out, not_8_out;

  not not_1 (not_1_out, c3);
  not not_2 (not_2_out, c1);
  not not_3 (not_3_out, c2);
  not not_4 (not_4_out, c0);
  not not_5 (not_5_out, c2);
  not not_6 (not_6_out, c0);
  not not_7 (not_7_out, c1);
  not not_8 (not_8_out, c0);
  and and_1 (and_1_out, not_1_out, not_3_out, not_4_out);
  and and_2 (and_2_out, not_5_out, c1, c0);
  and and_3 (and_3_out, c0, not_2_out, c2);
  and and_4 (and_4_out, not_6_out, not_7_out, c3);
  and and_5 (and_5_out, not_8_out, c1, c2);
  or or_1 (hex3, and_1_out, and_2_out, and_3_out, and_4_out, and_5_out);

  // Notes on the sheet:
  //   HEX[3]
endmodule

module hex_4 (
  input  c0,
  input  c1,
  input  c2,
  input  c3,
  output hex4
);

  wire and_1_out, and_2_out, and_3_out, and_4_out, not_1_out, not_2_out;

  not not_1 (not_1_out, c0);
  not not_2 (not_2_out, c2);
  and and_1 (and_1_out, not_1_out, not_2_out);
  and and_2 (and_2_out, not_1_out, c1);
  and and_3 (and_3_out, c2, c3);
  and and_4 (and_4_out, c1, c3);
  or or_1 (hex4, and_1_out, and_2_out, and_3_out, and_4_out);

  // Notes on the sheet:
  //   HEX[4]
endmodule

module hex_5 (
  input  c0,
  input  c1,
  input  c2,
  input  c3,
  output hex5
);

  wire and_1_out, and_2_out, and_3_out, and_4_out, and_5_out, not_1_out, not_2_out, not_3_out, not_4_out;

  not not_1 (not_1_out, c0);
  not not_2 (not_2_out, c1);
  not not_3 (not_3_out, c2);
  not not_4 (not_4_out, c3);
  and and_1 (and_1_out, not_1_out, not_2_out);
  and and_2 (and_2_out, not_1_out, c2);
  and and_3 (and_3_out, not_2_out, c2, not_4_out);
  and and_4 (and_4_out, not_3_out, c3);
  and and_5 (and_5_out, c1, c3);
  or or_1 (hex5, and_1_out, and_2_out, and_3_out, and_4_out, and_5_out);

  // Notes on the sheet:
  //   HEX[5]
endmodule

module hex_6 (
  input  c0,
  input  c1,
  input  c2,
  input  c3,
  output hex6
);

  wire and_1_out, and_2_out, and_3_out, and_4_out, and_5_out, not_1_out, not_2_out, not_3_out, not_4_out;

  not not_1 (not_1_out, c0);
  not not_2 (not_2_out, c1);
  not not_3 (not_3_out, c2);
  not not_4 (not_4_out, c3);
  and and_1 (and_1_out, not_3_out, c1);
  and and_2 (and_2_out, not_2_out, c2, not_4_out);
  and and_3 (and_3_out, c1, not_1_out);
  and and_4 (and_4_out, c3, c0);
  and and_5 (and_5_out, not_3_out, c3);
  or or_1 (hex6, and_1_out, and_2_out, and_3_out, and_4_out, and_5_out);

  // Notes on the sheet:
  //   HEX[6]
endmodule
