// Logisim project lab3_part1.circ as structural Verilog: 1 circuit, main circuit part1
module part1 (
  input  [9:0] SWs,
  output LEDR0
);

  Multiplexer #(.enable("false"), .select(3)) multiplexer_1 (
    .in0(SWs[9]), .in1(SWs[8]), .in2(SWs[7]), .in3(SWs[6]), .in4(SWs[5]), .in5(SWs[4]), .in6(SWs[3]),
    .out(LEDR0), .sel(SWs[2:0]));  // open: in7

  // Notes on the sheet:
  //   Part1
endmodule
