// Logisim project lab3_part2.circ as structural Verilog: 2 circuits, main circuit main
module main (
  input  SW8,
  input  [3:0] A_INPUT,
  input  [3:0] B_INPUT,
  output LEDR0,
  output LEDR1,
  output LEDR2,
  output LEDR4,
  output LEDR3
);

  wire FA1_cout, FA2_cout, FA3_cout;

  subcircuit FA1 (.A(A_INPUT[0]), .Cin(SW8), .B(B_INPUT[0]), .Cout(FA1_cout), .S(LEDR0));
  subcircuit FA2 (.A(A_INPUT[1]), .Cin(FA1_cout), .B(B_INPUT[1]), .Cout(FA2_cout), .S(LEDR1));
  subcircuit FA3 (.A(A_INPUT[2]), .Cin(FA2_cout), .B(B_INPUT[2]), .Cout(FA3_cout), .S(LEDR2));
  subcircuit FA4 (.A(A_INPUT[3]), .Cin(FA3_cout), .B(B_INPUT[3]), .Cout(LEDR4), .S(LEDR3));
endmodule

module subcircuit (
  input  A,
  input  Cin,
  input  B,
  output Cout,
  output S
);

  wire xor_1_out;

  Multiplexer #(.enable("false")) multiplexer_1 (.in0(B), .in1(Cin), .out(Cout), .sel(xor_1_out));
  xor xor_1 (xor_1_out, B, A);
  xor xor_2 (S, xor_1_out, Cin);
endmodule
