// Logisim project part1.circ as structural Verilog: 2 circuits, main circuit main
module main (
  input  D,
  input  Clk,
  output Q_used1,
  output Q,
  output Q2
);

  wire d_latch_1_qa, not_1_out;

  not not_1 (not_1_out, Clk);
  d_latch d_latch_1 (.D(D), .Clk(Clk), .Qa(d_latch_1_qa), .Qb(Q_used1));
  d_latch d_latch_2 (.D(d_latch_1_qa), .Clk(not_1_out), .Qa(Q), .Qb(Q2));
endmodule

module d_latch (
  input  D,
  input  Clk,
  output Qa,
  output Qb
);

  wire nand_1_out, nand_2_out, not_1_out;

  not not_1 (not_1_out, D);
  nand nand_1 (nand_1_out, D, Clk);
  nand nand_2 (nand_2_out, Clk, not_1_out);
  nand nand_3 (Qa, nand_1_out, Qb);
  nand nand_4 (Qb, Qa, nand_2_out);
endmodule
