// Logisim project part2.circ as structural Verilog: 23 circuits, main circuit main
module main (
  input  [3:0] Data,
  input  Clk,
  input  [2:0] S,
  output [7:0] TEST
);

  wire display1_hex0, display1_hex1, display1_hex2, display1_hex3, display1_hex4, display1_hex5,
       display1_hex6, display2_hex0, display2_hex1, display2_hex2, display2_hex3, display2_hex4,
       display2_hex5, display2_hex6, display_1_hex0, display_1_hex1, display_1_hex2, display_1_hex3,
       display_1_hex4, display_1_hex5, display_1_hex6;
  wire [3:0] bit_extender_1_out;
  wire [7:0] function0_1_aluout0, function1_1_aluout1, function2_1_aluout2, function3_1_aluout3,
       function4_1_aluout4, multiplexer_1_out, new_function_5_1_result, new_function_6_1_result,
       new_function_7_1_result;

  display display_1 (
    .c0(Data[0]), .c1(Data[1]), .c2(Data[2]), .c3(Data[3]), .hex0(display_1_hex0), .hex1(display_1_hex1),
    .hex2(display_1_hex2), .hex3(display_1_hex3), .hex4(display_1_hex4), .hex5(display_1_hex5),
    .hex6(display_1_hex6));
  _7_Segment_Display u_7_segment_display_1 (
    .g(display_1_hex6), .f(display_1_hex5), .a(display_1_hex0), .b(display_1_hex1), .e(display_1_hex4),
    .d(display_1_hex3), .c(display_1_hex2));  // open: dp
  function0 function0_1 (.A(Data), .ALUout0(function0_1_aluout0));
  function1 function1_1 (.A(Data), .B(bit_extender_1_out), .ALUout1(function1_1_aluout1));
  function2 function2_1 (.A(Data), .B(bit_extender_1_out), .ALUout2(function2_1_aluout2));
  function3 function3_1 (.A(Data), .B(bit_extender_1_out), .ALUout3(function3_1_aluout3));
  function4 function4_1 (.A(Data), .B(bit_extender_1_out), .ALUout4(function4_1_aluout4));
  new_function_5 new_function_5_1 (.B(bit_extender_1_out), .A(Data), .Result(new_function_5_1_result));
  new_function_6 new_function_6_1 (.B(bit_extender_1_out), .A(Data), .Result(new_function_6_1_result));
  new_function_7 new_function_7_1 (.A(Data), .B(bit_extender_1_out), .Result(new_function_7_1_result));
  Multiplexer #(.enable("false"), .select(3), .width(8)) multiplexer_1 (
    .in0(function0_1_aluout0), .in1(function1_1_aluout1), .in2(function2_1_aluout2),
    .in3(function3_1_aluout3), .in4(function4_1_aluout4), .in5(new_function_5_1_result),
    .in6(new_function_6_1_result), .in7(new_function_7_1_result), .out(multiplexer_1_out), .sel(S));
  Register register_1 (.D(multiplexer_1_out), .clk(Clk), .Q(TEST));  // open: en, clr
  Bit_Extender #(.out_width(4)) bit_extender_1 (.in(TEST), .out(bit_extender_1_out));
  LED LED6 (.in(TEST[6]));
  LED LED7 (.in(TEST[7]));
  LED LED5 (.in(TEST[5]));
  LED LED4 (.in(TEST[4]));
  LED LED3 (.in(TEST[3]));
  LED LED2 (.in(TEST[2]));
  display display2 (
    .c0(TEST[0]), .c1(TEST[1]), .c2(TEST[2]), .c3(TEST[3]), .hex0(display2_hex0), .hex1(display2_hex1),
    .hex2(display2_hex2), .hex3(display2_hex3), .hex4(display2_hex4), .hex5(display2_hex5),
    .hex6(display2_hex6));
  display display1 (
    .c0(TEST[4]), .c1(TEST[5]), .c2(TEST[6]), .c3(TEST[7]), .hex0(display1_hex0), .hex1(display1_hex1),
    .hex2(display1_hex2), .hex3(display1_hex3), .hex4(display1_hex4), .hex5(display1_hex5),
    .hex6(display1_hex6));
  LED LED1 (.in(TEST[1]));
  _7_Segment_Display u_7_segment_display_2 (
    .g(display1_hex6), .f(display1_hex5), .a(display1_hex0), .b(display1_hex1), .e(display1_hex4),
    .d(display1_hex3), .c(display1_hex2));  // open: dp
  LED LED0 (.in(TEST[0]));
  _7_Segment_Display u_7_segment_display_3 (
    .g(display2_hex6), .f(display2_hex5), .a(display2_hex0), .b(display2_hex1), .e(display2_hex4),
    .d(display2_hex3), .c(display2_hex2));  // open: dp
endmodule

module part1 (
  input  [9:0] SWs,
  output LEDR0
);

  Multiplexer #(.enable("false"), .select(3)) multiplexer_1 (
    .in0(SWs[9]), .in1(SWs[8]), .in2(SWs[7]), .in3(SWs[6]), .in4(SWs[5]), .in5(SWs[4]), .in6(SWs[3]),
    .out(LEDR0), .sel(SWs[2:0]));  // open: in7

  // Notes on the sheet:
  //   Part1
endmodule

module hex_0 (
  input  c0,
  input  c1,
  input  c2,
  input  c3,
  output hex0
);

  wire and_1_out, and_2_out, and_3_out, and_4_out, and_5_out, and_6_out, not_1_out, not_2_out, not_3_out,
       not_4_out;

  not not_1 (not_1_out, c0);
  not not_2 (not_2_out, c1);
  not not_3 (not_3_out, c2);
  not not_4 (not_4_out, c3);
  and and_1 (and_1_out, not_1_out, not_3_out);
  and and_2 (and_2_out, c1, not_4_out);
  and and_3 (and_3_out, not_4_out, c2, c0);
  and and_4 (and_4_out, c2, c1);
  and and_5 (and_5_out, c3, not_1_out);
  and and_6 (and_6_out, c3, not_2_out, not_3_out);
  or or_1 (hex0, and_1_out, and_2_out, and_3_out, and_4_out, and_5_out, and_6_out);

  // Notes on the sheet:
  //   HEX[0]
endmodule

module hex_1 (
  input  c0,
  input  c1,
  input  c2,
  input  c3,
  output hex1
);

  wire and_1_out, and_2_out, and_3_out, and_4_out, and_5_out, not_1_out, not_2_out, not_3_out, not_4_out;

  not not_1 (not_1_out, c0);
  not not_2 (not_2_out, c1);
  not not_3 (not_3_out, c2);
  not not_4 (not_4_out, c3);
  and and_1 (and_1_out, not_3_out, not_4_out);
  and and_2 (and_2_out, not_1_out, not_3_out);
  and and_3 (and_3_out, not_1_out, not_2_out, not_4_out);
  and and_4 (and_4_out, c0, not_2_out, c3);
  and and_5 (and_5_out, c0, c1, not_4_out);
  or or_1 (hex1, and_1_out, and_2_out, and_3_out, and_4_out, and_5_out);

  // Notes on the sheet:
  //   HEX[1]
endmodule

module hex_2 (
  input  c0,
  input  c1,
  input  c2,
  input  c3,
  output hex2
);

  wire and_1_out, and_2_out, and_3_out, and_4_out, and_5_out, not_1_out, not_2_out, not_3_out;

  not not_1 (not_1_out, c1);
  not not_2 (not_2_out, c2);
  not not_3 (not_3_out, c3);
  and and_1 (and_1_out, not_1_out, not_3_out);
  and and_2 (and_2_out, c0, not_3_out);
  and and_3 (and_3_out, not_1_out, c0);
  and and_4 (and_4_out, c2, not_3_out);
  and and_5 (and_5_out, not_2_out, c3);
  or or_1 (hex2, and_1_out, and_2_out, and_3_out, and_4_out, and_5_out);

  // Notes on the sheet:
  //   HEX[2]
endmodule

module hex_3 (
  input  c0,
  input  c1,
  input  c2,
  input  c3,
  output hex3
);

  wire and_1_out, and_2_out, and_3_out, and_4_out, and_5_out, not_1_out, not_2_out, not_3_out, not_4_out,
       not_5_out, not_6_out, not_7_out, not_8_out;

  not not_1 (not_1_out, c3);
  not not_2 (not_2_out, c1);
  not not_3 (not_3_out, c2);
  not not_4 (not_4_out, c0);
  not not_5 (not_5_out, c2);
  not not_6 (not_6_out, c0);
  not not_7 (not_7_out, c1);
  not not_8 (not_8_out, c0);
  and and_1 (and_1_out, not_1_out, not_3_out, not_4_out);
  and and_2 (and_2_out, not_5_out, c1, c0);
  and and_3 (and_3_out, c0, not_2_out, c2);
  and and_4 (and_4_out, not_6_out, not_7_out, c3);
  and and_5 (and_5_out, not_8_out, c1, c2);
  or or_1 (hex3, and_1_out, and_2_out, and_3_out, and_4_out, and_5_out);

  // Notes on the sheet:
  //   HEX[3]
endmodule

module hex_4 (
  input  c0,
  input  c1,
  input  c2,
  input  c3,
  output hex4
);

  wire and_1_out, and_2_out, and_3_out, and_4_out, not_1_out, not_2_out;

  not not_1 (not_1_out, c0);
  not not_2 (not_2_out, c2);
  and and_1 (and_1_out, not_1_out, not_2_out);
  and and_2 (and_2_out, not_1_out, c1);
  and and_3 (and_3_out, c2, c3);
  and and_4 (and_4_out, c1, c3);
  or or_1 (hex4, and_1_out, and_2_out, and_3_out, and_4_out);

  // Notes on the sheet:
  //   HEX[4]
endmodule

module hex_5 (
  input  c0,
  input  c1,
  input  c2,
  input  c3,
  output hex5
);

  wire and_1_out, and_2_out, and_3_out, and_4_out, and_5_out, not_1_out, not_2_out, not_3_out, not_4_out;

  not not_1 (not_1_out, c0);
  not not_2 (not_2_out, c1);
  not not_3 (not_3_out, c2);
  not not_4 (not_4_out, c3);
  and and_1 (and_1_out, not_1_out, not_2_out);
  and and_2 (and_2_out, not_1_out, c2);
  and and_3 (and_3_out, not_2_out, c2, not_4_out);
  and and_4 (and_4_out, not_3_out, c3);
  and and_5 (and_5_out, c1, c3);
  or or_1 (hex5, and_1_out, and_2_out, and_3_out, and_4_out, and_5_out);

  // Notes on the sheet:
  //   HEX[5]
endmodule

module hex_6 (
  input  c0,
  input  c1,
  input  c2,
  input  c3,
  output hex6
);

  wire and_1_out, and_2_out, and_3_out, and_4_out, and_5_out, not_1_out, not_2_out, not_3_out, not_4_out;

  not not_1 (not_1_out, c0);
  not not_2 (not_2_out, c1);
  not not_3 (not_3_out, c2);
  not not_4 (not_4_out, c3);
  and and_1 (and_1_out, not_3_out, c1);
  and and_2 (and_2_out, not_2_out, c2, not_4_out);
  and and_3 (and_3_out, c1, not_1_out);
  and and_4 (and_4_out, c3, c0);
  and and_5 (and_5_out, not_3_out, c3);
  or or_1 (hex6, and_1_out, and_2_out, and_3_out, and_4_out, and_5_out);

  // Notes on the sheet:
  //   HEX[6]
endmodule

module subcircuit (
  input  A,
  input  Cin,
  input  B,
  output Cout,
  output S
);

  wire xor_1_out;

  Multiplexer #(.enable("false")) multiplexer_1 (.in0(B), .in1(Cin), .out(Cout), .sel(xor_1_out));
  xor xor_1 (xor_1_out, B, A);
  xor xor_2 (S, xor_1_out, Cin);
endmodule

module four_full_adder (
  input  SW8,
  input  [3:0] A_INPUT,
  input  [3:0] B_INPUT,
  output LEDR0,
  output LEDR1,
  output LEDR2,
  output LEDR4,
  output out_8
);

  wire FA1_cout, FA2_cout, FA3_cout;

  subcircuit FA1 (.A(A_INPUT[0]), .Cin(SW8), .B(B_INPUT[0]), .Cout(FA1_cout), .S(LEDR0));
  subcircuit FA2 (.A(A_INPUT[1]), .Cin(FA1_cout), .B(B_INPUT[1]), .Cout(FA2_cout), .S(LEDR1));
  subcircuit FA3 (.A(A_INPUT[2]), .Cin(FA2_cout), .B(B_INPUT[2]), .Cout(FA3_cout), .S(LEDR2));
  subcircuit FA4 (.A(A_INPUT[3]), .Cin(FA3_cout), .B(B_INPUT[3]), .Cout(LEDR4), .S(out_8));
endmodule

module function0 (
  input  [3:0] A,
  output [7:0] ALUout0
);

  wire [4:0] lab3_part2_1_ledr0;

  lab3_part2 lab3_part2_1 (
    .SW8(1'b0), .A_INPUT(A), .B_INPUT(4'b0001), .LEDR0(lab3_part2_1_ledr0[0]), .LEDR1(lab3_part2_1_ledr0[1]),
    .LEDR2(lab3_part2_1_ledr0[2]), .LEDR4(lab3_part2_1_ledr0[4]), .LEDR3(lab3_part2_1_ledr0[3]));
  assign ALUout0 = {{3{1'b0}}, lab3_part2_1_ledr0};  // Bit_Extender bit_extender_1
endmodule

module function1 (
  input  [3:0] A,
  input  [3:0] B,
  output [7:0] ALUout1
);

  wire [4:0] lab3_part2_1_ledr0;

  lab3_part2 lab3_part2_1 (
    .SW8(1'b0), .A_INPUT(A), .B_INPUT(B), .LEDR0(lab3_part2_1_ledr0[0]), .LEDR1(lab3_part2_1_ledr0[1]),
    .LEDR2(lab3_part2_1_ledr0[2]), .LEDR4(lab3_part2_1_ledr0[4]), .LEDR3(lab3_part2_1_ledr0[3]));
  assign ALUout1 = {{3{1'b0}}, lab3_part2_1_ledr0};  // Bit_Extender bit_extender_1
endmodule

module function2 (
  input  [3:0] A,
  input  [3:0] B,
  output [7:0] ALUout2
);

  wire [3:0] adder_1_out;
  wire [4:4] adder_1_cout;

  Adder #(.width(4)) adder_1 (.a(A), .b(B), .out(adder_1_out), .cin(1'b0), .cout(adder_1_cout[4]));
  assign ALUout2 = {{3{1'b0}}, {adder_1_cout[4], adder_1_out}};  // Bit_Extender bit_extender_1
endmodule

module function3 (
  input  [3:0] A,
  input  [3:0] B,
  output [7:0] ALUout3
);

  assign ALUout3[3:0] = A ^ B;  // XOR_Gate xor_1, 4 bits wide
  assign ALUout3[7:4] = A | B;  // OR_Gate or_1, 4 bits wide
endmodule

module function4 (
  input  [3:0] A,
  input  [3:0] B,
  output [7:0] ALUout4
);

  wire or_1_out;

  assign ALUout4 = {{7{1'b0}}, or_1_out};  // Bit_Extender bit_extender_1
  or or_1 (or_1_out, A[0], A[1], A[2], A[3], B[0], B[1], B[2], B[3]);
endmodule

module function5 (
  input  [3:0] A,
  input  [3:0] B,
  output [7:0] AULout5
);


  assign AULout5 = {A, B};
endmodule

module lab3_part2 (
  input  SW8,
  input  [3:0] A_INPUT,
  input  [3:0] B_INPUT,
  output LEDR0,
  output LEDR1,
  output LEDR2,
  output LEDR4,
  output LEDR3
);

  wire FA1_cout, FA2_cout, FA3_cout;

  subcircuit FA1 (.A(A_INPUT[0]), .Cin(SW8), .B(B_INPUT[0]), .Cout(FA1_cout), .S(LEDR0));
  subcircuit FA2 (.A(A_INPUT[1]), .Cin(FA1_cout), .B(B_INPUT[1]), .Cout(FA2_cout), .S(LEDR1));
  subcircuit FA3 (.A(A_INPUT[2]), .Cin(FA2_cout), .B(B_INPUT[2]), .Cout(FA3_cout), .S(LEDR2));
  subcircuit FA4 (.A(A_INPUT[3]), .Cin(FA3_cout), .B(B_INPUT[3]), .Cout(LEDR4), .S(LEDR3));
endmodule

module display (
  input  c0,
  input  c1,
  input  c2,
  input  c3,
  output hex0,
  output hex1,
  output hex2,
  output hex3,
  output hex4,
  output hex5,
  output hex6
);

  hex_0 hex_0_1 (.c0(c0), .c1(c1), .c2(c2), .c3(c3), .hex0(hex0));
  hex_1 hex_1_1 (.c0(c0), .c1(c1), .c2(c2), .c3(c3), .hex1(hex1));
  hex_2 hex_2_1 (.c0(c0), .c1(c1), .c2(c2), .c3(c3), .hex2(hex2));
  hex_3 hex_3_1 (.c0(c0), .c1(c1), .c2(c2), .c3(c3), .hex3(hex3));
  hex_4 hex_4_1 (.c0(c0), .c1(c1), .c2(c2), .c3(c3), .hex4(hex4));
  hex_5 hex_5_1 (.c0(c0), .c1(c1), .c2(c2), .c3(c3), .hex5(hex5));
  hex_6 hex_6_1 (.c0(c0), .c1(c1), .c2(c2), .c3(c3), .hex6(hex6));
endmodule

module lab3_part3_main (
  input  [3:0] A,
  input  [3:0] B,
  input  [2:0] S,
  output [7:0] TEST
);

  wire D1_hex0, D1_hex1, D1_hex2, D1_hex3, D1_hex4, D1_hex5, D1_hex6, D2_hex0, D2_hex1, D2_hex2, D2_hex3,
       D2_hex4, D2_hex5, D2_hex6, D3_hex0, D3_hex1, D3_hex2, D3_hex3, D3_hex4, D3_hex5, D3_hex6, D4_hex0,
       D4_hex1, D4_hex2, D4_hex3, D4_hex4, D4_hex5, D4_hex6;
  wire [7:0] F0_aluout0, F1_aluout1, F2_aluout2, F3_aluout3, F4_aluout4, F5_aulout5;

  display D1 (
    .c0(A[0]), .c1(A[1]), .c2(A[2]), .c3(A[3]), .hex0(D1_hex0), .hex1(D1_hex1), .hex2(D1_hex2),
    .hex3(D1_hex3), .hex4(D1_hex4), .hex5(D1_hex5), .hex6(D1_hex6));
  display D2 (
    .c0(B[0]), .c1(B[1]), .c2(B[2]), .c3(B[3]), .hex0(D2_hex0), .hex1(D2_hex1), .hex2(D2_hex2),
    .hex3(D2_hex3), .hex4(D2_hex4), .hex5(D2_hex5), .hex6(D2_hex6));
  _7_Segment_Display u_7_segment_display_1 (
    .g(D1_hex6), .f(D1_hex5), .a(D1_hex0), .b(D1_hex1), .e(D1_hex4), .d(D1_hex3), .c(D1_hex2));  // open: dp
  _7_Segment_Display u_7_segment_display_2 (
    .g(D2_hex6), .f(D2_hex5), .a(D2_hex0), .b(D2_hex1), .e(D2_hex4), .d(D2_hex3), .c(D2_hex2));  // open: dp
  function0 F0 (.A(A), .ALUout0(F0_aluout0));
  function1 F1 (.A(A), .B(B), .ALUout1(F1_aluout1));
  function2 F2 (.A(A), .B(B), .ALUout2(F2_aluout2));
  function3 F3 (.A(A), .B(B), .ALUout3(F3_aluout3));
  function4 F4 (.A(A), .B(B), .ALUout4(F4_aluout4));
  function5 F5 (.A(A), .B(B), .AULout5(F5_aulout5));
  Multiplexer #(.enable("false"), .select(3), .width(8)) multiplexer_1 (
    .in0(F0_aluout0), .in1(F1_aluout1), .in2(F2_aluout2), .in3(F3_aluout3), .in4(F4_aluout4),
    .in5(F5_aulout5), .out(TEST), .sel(S));  // open: in6, in7
  LED LED7 (.in(TEST[7]));
  LED LED6 (.in(TEST[6]));
  LED LED5 (.in(TEST[5]));
  LED LED4 (.in(TEST[4]));
  LED LED3 (.in(TEST[3]));
  LED LED2 (.in(TEST[2]));
  display D3 (
    .c0(TEST[0]), .c1(TEST[1]), .c2(TEST[2]), .c3(TEST[3]), .hex0(D3_hex0), .hex1(D3_hex1), .hex2(D3_hex2),
    .hex3(D3_hex3), .hex4(D3_hex4), .hex5(D3_hex5), .hex6(D3_hex6));
  display D4 (
    .c0(TEST[4]), .c1(TEST[5]), .c2(TEST[6]), .c3(TEST[7]), .hex0(D4_hex0), .hex1(D4_hex1), .hex2(D4_hex2),
    .hex3(D4_hex3), .hex4(D4_hex4), .hex5(D4_hex5), .hex6(D4_hex6));
  LED LED1 (.in(TEST[1]));
  LED LED0 (.in(TEST[0]));
  _7_Segment_Display u_7_segment_display_3 (
    .g(D4_hex6), .f(D4_hex5), .a(D4_hex0), .b(D4_hex1), .e(D4_hex4), .d(D4_hex3), .c(D4_hex2));  // open: dp
  _7_Segment_Display u_7_segment_display_4 (
    .g(D3_hex6), .f(D3_hex5), .a(D3_hex0), .b(D3_hex1), .e(D3_hex4), .d(D3_hex3), .c(D3_hex2));  // open: dp
endmodule

module new_function_5 (
  input  [3:0] B,
  input  [3:0] A,
  output [7:0] Result
);

  wire [8:0] bit_extender_1_out, shifter_1_out;

  assign bit_extender_1_out = {{5{1'b0}}, B};  // Bit_Extender bit_extender_1
  Shifter #(.width(9)) shifter_1 (.in(bit_extender_1_out), .\dist (A), .out(shifter_1_out));
  Bit_Extender #(.in_width(9), .out_width(8), .\type ("zero")) bit_extender_2 (.in(shifter_1_out), .out(Result));
endmodule

module new_function_6 (
  input  [3:0] B,
  input  [3:0] A,
  output [7:0] Result
);

  wire [8:0] bit_extender_1_out, shifter_1_out;

  assign bit_extender_1_out = {{5{1'b0}}, B};  // Bit_Extender bit_extender_1
  Shifter #(.shift("lr"), .width(9)) shifter_1 (.in(bit_extender_1_out), .\dist (A), .out(shifter_1_out));
  Bit_Extender #(.in_width(9), .out_width(8), .\type ("zero")) bit_extender_2 (.in(shifter_1_out), .out(Result));
endmodule

module new_function_7 (
  input  [3:0] A,
  input  [3:0] B,
  output [7:0] Result
);

  Multiplier #(.width(4)) multiplier_1 (.a(A), .b(B), .out(Result[3:0]), .cout(Result[7:4]));  // open: cin
endmodule
