// Logisim project part3.circ as structural Verilog: 2 circuits, main circuit main
module main (
  input  [7:0] LoadVal,
  input  Load_n,
  input  ShiftRight,
  input  ASR,
  input  clk,
  input  reset,
  output [7:0] Q
);

  wire multiplexer_1_out;

  Multiplexer #(.enable("false")) multiplexer_1 (.in0(1'b0), .in1(LoadVal[7]), .out(multiplexer_1_out), .sel(ASR));
  ShiftBit S0 (
    .load_val(LoadVal[0]), .in_port(Q[1]), .clk(clk), .shift(ShiftRight), .reset(reset), .load_n(Load_n),
    .out_put(Q[0]));
  ShiftBit S1 (
    .load_val(LoadVal[1]), .in_port(Q[2]), .clk(clk), .shift(ShiftRight), .reset(reset), .load_n(Load_n),
    .out_put(Q[1]));
  ShiftBit S2 (
    .load_val(LoadVal[2]), .in_port(Q[3]), .clk(clk), .shift(ShiftRight), .reset(reset), .load_n(Load_n),
    .out_put(Q[2]));
  ShiftBit S3 (
    .load_val(LoadVal[3]), .in_port(Q[4]), .clk(clk), .shift(ShiftRight), .reset(reset), .load_n(Load_n),
    .out_put(Q[3]));
  ShiftBit S4 (
    .load_val(LoadVal[4]), .in_port(Q[5]), .clk(clk), .shift(ShiftRight), .reset(reset), .load_n(Load_n),
    .out_put(Q[4]));
  ShiftBit S5 (
    .load_val(LoadVal[5]), .in_port(Q[6]), .clk(clk), .shift(ShiftRight), .reset(reset), .load_n(Load_n),
    .out_put(Q[5]));
  ShiftBit S6 (
    .load_val(LoadVal[6]), .in_port(Q[7]), .clk(clk), .shift(ShiftRight), .reset(reset), .load_n(Load_n),
    .out_put(Q[6]));
  ShiftBit S7 (
    .load_val(LoadVal[7]), .in_port(multiplexer_1_out), .clk(clk), .shift(ShiftRight), .reset(reset),
    .load_n(Load_n), .out_put(Q[7]));
endmodule

module ShiftBit (
  input  load_val,
  input  in_port,
  input  clk,
  input  shift,
  input  reset,
  input  load_n,
  output out_put
);

  wire multiplexer_1_out, multiplexer_2_out;

  Multiplexer #(.enable("false")) multiplexer_1 (.in0(out_put), .in1(in_port), .out(multiplexer_1_out), .sel(shift));
  Multiplexer #(.enable("false")) multiplexer_2 (
    .in0(load_val), .in1(multiplexer_1_out), .out(multiplexer_2_out), .sel(load_n));
  D_Flip_Flop d_ff_1 (.D(multiplexer_2_out), .clk(clk), .Q(out_put), .reset(reset));  // open: Qn, preset
endmodule
