// Logisim project lab5_part1.circ as structural Verilog: 18 circuits, main circuit main
module main (
  input  Enable,
  input  Clock,
  input  Clear_b
);

  wire and_1_out, and_2_out, and_3_out, and_4_out, and_5_out, and_6_out, and_7_out, display_1_hex0,
       display_1_hex1, display_1_hex2, display_1_hex3, display_1_hex4, display_1_hex5, display_1_hex6,
       display_2_hex0, display_2_hex1, display_2_hex2, display_2_hex3, display_2_hex4, display_2_hex5,
       display_2_hex6, not_1_out, not_2_out, not_3_out, not_4_out, not_5_out, not_6_out, not_7_out,
       not_8_out, t_ff_1_q, t_ff_2_q, t_ff_3_q, t_ff_4_q, t_ff_5_q, t_ff_6_q, t_ff_7_q, t_ff_8_q;

  T_Flip_Flop t_ff_1 (.T(Enable), .clk(Clock), .Q(t_ff_1_q), .reset(not_1_out));  // open: Qn, preset
  not not_1 (not_1_out, Clear_b);
  and and_1 (and_1_out, Enable, t_ff_1_q);
  T_Flip_Flop t_ff_2 (.T(and_1_out), .clk(Clock), .Q(t_ff_2_q), .reset(not_2_out));  // open: Qn, preset
  not not_2 (not_2_out, Clear_b);
  display display_1 (
    .c0(t_ff_5_q), .c1(t_ff_6_q), .c2(t_ff_7_q), .c3(t_ff_8_q), .hex0(display_1_hex0), .hex1(display_1_hex1),
    .hex2(display_1_hex2), .hex3(display_1_hex3), .hex4(display_1_hex4), .hex5(display_1_hex5),
    .hex6(display_1_hex6));
  and and_2 (and_2_out, and_1_out, t_ff_2_q);
  _7_Segment_Display u_7_segment_display_1 (
    .g(display_1_hex6), .f(display_1_hex5), .a(display_1_hex0), .b(display_1_hex1), .e(display_1_hex4),
    .d(display_1_hex3), .c(display_1_hex2));  // open: dp
  T_Flip_Flop t_ff_3 (.T(and_2_out), .clk(Clock), .Q(t_ff_3_q), .reset(not_3_out));  // open: Qn, preset
  not not_3 (not_3_out, Clear_b);
  and and_3 (and_3_out, and_2_out, t_ff_3_q);
  T_Flip_Flop t_ff_4 (.T(and_3_out), .clk(Clock), .Q(t_ff_4_q), .reset(not_4_out));  // open: Qn, preset
  not not_4 (not_4_out, Clear_b);
  and and_4 (and_4_out, and_3_out, t_ff_4_q);
  T_Flip_Flop t_ff_5 (.T(and_4_out), .clk(Clock), .Q(t_ff_5_q), .reset(not_5_out));  // open: Qn, preset
  not not_5 (not_5_out, Clear_b);
  display display_2 (
    .c0(t_ff_1_q), .c1(t_ff_2_q), .c2(t_ff_3_q), .c3(t_ff_4_q), .hex0(display_2_hex0), .hex1(display_2_hex1),
    .hex2(display_2_hex2), .hex3(display_2_hex3), .hex4(display_2_hex4), .hex5(display_2_hex5),
    .hex6(display_2_hex6));
  _7_Segment_Display u_7_segment_display_2 (
    .g(display_2_hex6), .f(display_2_hex5), .a(display_2_hex0), .b(display_2_hex1), .e(display_2_hex4),
    .d(display_2_hex3), .c(display_2_hex2));  // open: dp
  and and_5 (and_5_out, and_4_out, t_ff_5_q);
  T_Flip_Flop t_ff_6 (.T(and_5_out), .clk(Clock), .Q(t_ff_6_q), .reset(not_6_out));  // open: Qn, preset
  not not_6 (not_6_out, Clear_b);
  and and_6 (and_6_out, and_5_out, t_ff_6_q);
  T_Flip_Flop t_ff_7 (.T(and_6_out), .clk(Clock), .Q(t_ff_7_q), .reset(not_7_out));  // open: Qn, preset
  not not_7 (not_7_out, Clear_b);
  and and_7 (and_7_out, and_6_out, t_ff_7_q);
  T_Flip_Flop t_ff_8 (.T(and_7_out), .clk(Clock), .Q(t_ff_8_q), .reset(not_8_out));  // open: Qn, preset
  not not_8 (not_8_out, Clear_b);
endmodule

module a (
  input  Enable,
  input  Clock,
  input  Clear_b
);

  wire and_1_out, and_2_out, and_3_out, and_4_out, and_5_out, and_6_out, and_7_out, display_1_hex0,
       display_1_hex1, display_1_hex2, display_1_hex3, display_1_hex4, display_1_hex5, display_1_hex6,
       display_2_hex0, display_2_hex1, display_2_hex2, display_2_hex3, display_2_hex4, display_2_hex5,
       display_2_hex6, not_1_out, not_2_out, not_3_out, not_4_out, not_5_out, not_6_out, not_7_out, t_ff_1_q,
       t_ff_2_q, t_ff_3_q, t_ff_4_q, t_ff_5_q, t_ff_6_q, t_ff_7_q, t_ff_8_q;

  T_Flip_Flop t_ff_1 (.T(Enable), .clk(Clock), .Q(t_ff_1_q), .reset(not_1_out));  // open: Qn, preset
  not not_1 (not_1_out, Clear_b);
  and and_1 (and_1_out, Enable, t_ff_1_q);
  T_Flip_Flop t_ff_2 (.T(and_1_out), .clk(Clock), .Q(t_ff_2_q), .reset(not_2_out));  // open: Qn, preset
  not not_2 (not_2_out, Clear_b);
  display display_1 (
    .c0(t_ff_5_q), .c1(t_ff_6_q), .c2(t_ff_7_q), .c3(t_ff_8_q), .hex0(display_1_hex0), .hex1(display_1_hex1),
    .hex2(display_1_hex2), .hex3(display_1_hex3), .hex4(display_1_hex4), .hex5(display_1_hex5),
    .hex6(display_1_hex6));
  and and_2 (and_2_out, and_1_out, t_ff_2_q);
  T_Flip_Flop t_ff_3 (.T(and_2_out), .clk(Clock), .Q(t_ff_3_q), .reset(Clear_b));  // open: Qn, preset
  _7_Segment_Display u_7_segment_display_1 (
    .g(display_1_hex6), .f(display_1_hex5), .a(display_1_hex0), .b(display_1_hex1), .e(display_1_hex4),
    .d(display_1_hex3), .c(display_1_hex2));  // open: dp
  and and_3 (and_3_out, and_2_out, t_ff_3_q);
  T_Flip_Flop t_ff_4 (.T(and_3_out), .clk(Clock), .Q(t_ff_4_q), .reset(not_3_out));  // open: Qn, preset
  not not_3 (not_3_out, Clear_b);
  and and_4 (and_4_out, and_3_out, t_ff_4_q);
  T_Flip_Flop t_ff_5 (.T(and_4_out), .clk(Clock), .Q(t_ff_5_q), .reset(not_4_out));  // open: Qn, preset
  not not_4 (not_4_out, Clear_b);
  and and_5 (and_5_out, and_4_out, t_ff_5_q);
  T_Flip_Flop t_ff_6 (.T(and_5_out), .clk(Clock), .Q(t_ff_6_q), .reset(not_5_out));  // open: Qn, preset
  not not_5 (not_5_out, Clear_b);
  display display_2 (
    .c0(t_ff_1_q), .c1(t_ff_2_q), .c2(t_ff_3_q), .c3(t_ff_4_q), .hex0(display_2_hex0), .hex1(display_2_hex1),
    .hex2(display_2_hex2), .hex3(display_2_hex3), .hex4(display_2_hex4), .hex5(display_2_hex5),
    .hex6(display_2_hex6));
  _7_Segment_Display u_7_segment_display_2 (
    .g(display_2_hex6), .f(display_2_hex5), .a(display_2_hex0), .b(display_2_hex1), .e(display_2_hex4),
    .d(display_2_hex3), .c(display_2_hex2));  // open: dp
  and and_6 (and_6_out, and_5_out, t_ff_6_q);
  T_Flip_Flop t_ff_7 (.T(and_6_out), .clk(Clock), .Q(t_ff_7_q), .reset(not_6_out));  // open: Qn, preset
  not not_6 (not_6_out, Clear_b);
  and and_7 (and_7_out, and_6_out, t_ff_7_q);
  T_Flip_Flop t_ff_8 (.T(and_7_out), .clk(Clock), .Q(t_ff_8_q), .reset(not_7_out));  // open: Qn, preset
  not not_7 (not_7_out, Clear_b);
endmodule

module hex_0 (
  input  c0,
  input  c1,
  input  c2,
  input  c3,
  output hex0
);

  wire and_1_out, and_2_out, and_3_out, and_4_out, and_5_out, and_6_out, not_1_out, not_2_out, not_3_out,
       not_4_out;

  not not_1 (not_1_out, c0);
  not not_2 (not_2_out, c1);
  not not_3 (not_3_out, c2);
  not not_4 (not_4_out, c3);
  and and_1 (and_1_out, not_1_out, not_3_out);
  and and_2 (and_2_out, c1, not_4_out);
  and and_3 (and_3_out, not_4_out, c2, c0);
  and and_4 (and_4_out, c2, c1);
  and and_5 (and_5_out, c3, not_1_out);
  and and_6 (and_6_out, c3, not_2_out, not_3_out);
  or or_1 (hex0, and_1_out, and_2_out, and_3_out, and_4_out, and_5_out, and_6_out);

  // Notes on the sheet:
  //   HEX[0]
endmodule

module hex_1 (
  input  c0,
  input  c1,
  input  c2,
  input  c3,
  output hex1
);

  wire and_1_out, and_2_out, and_3_out, and_4_out, and_5_out, not_1_out, not_2_out, not_3_out, not_4_out;

  not not_1 (not_1_out, c0);
  not not_2 (not_2_out, c1);
  not not_3 (not_3_out, c2);
  not not_4 (not_4_out, c3);
  and and_1 (and_1_out, not_3_out, not_4_out);
  and and_2 (and_2_out, not_1_out, not_3_out);
  and and_3 (and_3_out, not_1_out, not_2_out, not_4_out);
  and and_4 (and_4_out, c0, not_2_out, c3);
  and and_5 (and_5_out, c0, c1, not_4_out);
  or or_1 (hex1, and_1_out, and_2_out, and_3_out, and_4_out, and_5_out);

  // Notes on the sheet:
  //   HEX[1]
endmodule

module hex_2 (
  input  c0,
  input  c1,
  input  c2,
  input  c3,
  output hex2
);

  wire and_1_out, and_2_out, and_3_out, and_4_out, and_5_out, not_1_out, not_2_out, not_3_out;

  not not_1 (not_1_out, c1);
  not not_2 (not_2_out, c2);
  not not_3 (not_3_out, c3);
  and and_1 (and_1_out, not_1_out, not_3_out);
  and and_2 (and_2_out, c0, not_3_out);
  and and_3 (and_3_out, not_1_out, c0);
  and and_4 (and_4_out, c2, not_3_out);
  and and_5 (and_5_out, not_2_out, c3);
  or or_1 (hex2, and_1_out, and_2_out, and_3_out, and_4_out, and_5_out);

  // Notes on the sheet:
  //   HEX[2]
endmodule

module hex_3 (
  input  c0,
  input  c1,
  input  c2,
  input  c3,
  output hex3
);

  wire and_1_out, and_2_out, and_3_out, and_4_out, and_5_out, not_1_out, not_2_out, not_3_out, not_4_out,
       not_5_out, not_6_out, not_7_out, not_8_out;

  not not_1 (not_1_out, c3);
  not not_2 (not_2_out, c1);
  not not_3 (not_3_out, c2);
  not not_4 (not_4_out, c0);
  not not_5 (not_5_out, c2);
  not not_6 (not_6_out, c0);
  not not_7 (not_7_out, c1);
  not not_8 (not_8_out, c0);
  and and_1 (and_1_out, not_1_out, not_3_out, not_4_out);
  and and_2 (and_2_out, not_5_out, c1, c0);
  and and_3 (and_3_out, c0, not_2_out, c2);
  and and_4 (and_4_out, not_6_out, not_7_out, c3);
  and and_5 (and_5_out, not_8_out, c1, c2);
  or or_1 (hex3, and_1_out, and_2_out, and_3_out, and_4_out, and_5_out);

  // Notes on the sheet:
  //   HEX[3]
endmodule

module hex_4 (
  input  c0,
  input  c1,
  input  c2,
  input  c3,
  output hex4
);

  wire and_1_out, and_2_out, and_3_out, and_4_out, not_1_out, not_2_out;

  not not_1 (not_1_out, c0);
  not not_2 (not_2_out, c2);
  and and_1 (and_1_out, not_1_out, not_2_out);
  and and_2 (and_2_out, not_1_out, c1);
  and and_3 (and_3_out, c2, c3);
  and and_4 (and_4_out, c1, c3);
  or or_1 (hex4, and_1_out, and_2_out, and_3_out, and_4_out);

  // Notes on the sheet:
  //   HEX[4]
endmodule

module hex_5 (
  input  c0,
  input  c1,
  input  c2,
  input  c3,
  output hex5
);

  wire and_1_out, and_2_out, and_3_out, and_4_out, and_5_out, not_1_out, not_2_out, not_3_out, not_4_out;

  not not_1 (not_1_out, c0);
  not not_2 (not_2_out, c1);
  not not_3 (not_3_out, c2);
  not not_4 (not_4_out, c3);
  and and_1 (and_1_out, not_1_out, not_2_out);
  and and_2 (and_2_out, not_1_out, c2);
  and and_3 (and_3_out, not_2_out, c2, not_4_out);
  and and_4 (and_4_out, not_3_out, c3);
  and and_5 (and_5_out, c1, c3);
  or or_1 (hex5, and_1_out, and_2_out, and_3_out, and_4_out, and_5_out);

  // Notes on the sheet:
  //   HEX[5]
endmodule

module hex_6 (
  input  c0,
  input  c1,
  input  c2,
  input  c3,
  output hex6
);

  wire and_1_out, and_2_out, and_3_out, and_4_out, and_5_out, not_1_out, not_2_out, not_3_out, not_4_out;

  not not_1 (not_1_out, c0);
  not not_2 (not_2_out, c1);
  not not_3 (not_3_out, c2);
  not not_4 (not_4_out, c3);
  and and_1 (and_1_out, not_3_out, c1);
  and and_2 (and_2_out, not_2_out, c2, not_4_out);
  and and_3 (and_3_out, c1, not_1_out);
  and and_4 (and_4_out, c3, c0);
  and and_5 (and_5_out, not_3_out, c3);
  or or_1 (hex6, and_1_out, and_2_out, and_3_out, and_4_out, and_5_out);

  // Notes on the sheet:
  //   HEX[6]
endmodule

module subcircuit (
  input  A,
  input  Cin,
  input  B,
  output Cout,
  output S
);

  wire xor_1_out;

  Multiplexer #(.enable("false")) multiplexer_1 (.in0(B), .in1(Cin), .out(Cout), .sel(xor_1_out));
  xor xor_1 (xor_1_out, B, A);
  xor xor_2 (S, xor_1_out, Cin);
endmodule

module function0 (
  input  [3:0] A,
  output [7:0] ALUout0
);

  wire [4:0] lab3_part2_1_ledr0;

  lab3_part2 lab3_part2_1 (
    .SW8(1'b0), .A_INPUT(A), .B_INPUT(4'b0001), .LEDR0(lab3_part2_1_ledr0[0]), .LEDR1(lab3_part2_1_ledr0[1]),
    .LEDR2(lab3_part2_1_ledr0[2]), .LEDR4(lab3_part2_1_ledr0[4]), .LEDR3(lab3_part2_1_ledr0[3]));
  assign ALUout0 = {{3{1'b0}}, lab3_part2_1_ledr0};  // Bit_Extender bit_extender_1
endmodule

module function1 (
  input  [3:0] A,
  input  [3:0] B,
  output [7:0] ALUout1
);

  wire [4:0] lab3_part2_1_ledr0;

  lab3_part2 lab3_part2_1 (
    .SW8(1'b0), .A_INPUT(A), .B_INPUT(B), .LEDR0(lab3_part2_1_ledr0[0]), .LEDR1(lab3_part2_1_ledr0[1]),
    .LEDR2(lab3_part2_1_ledr0[2]), .LEDR4(lab3_part2_1_ledr0[4]), .LEDR3(lab3_part2_1_ledr0[3]));
  assign ALUout1 = {{3{1'b0}}, lab3_part2_1_ledr0};  // Bit_Extender bit_extender_1
endmodule

module function2 (
  input  [3:0] A,
  input  [3:0] B,
  output [7:0] ALUout2
);

  wire [3:0] adder_1_out;
  wire [4:4] adder_1_cout;

  Adder #(.width(4)) adder_1 (.a(A), .b(B), .out(adder_1_out), .cin(1'b0), .cout(adder_1_cout[4]));
  assign ALUout2 = {{3{1'b0}}, {adder_1_cout[4], adder_1_out}};  // Bit_Extender bit_extender_1
endmodule

module function3 (
  input  [3:0] A,
  input  [3:0] B,
  output [7:0] ALUout3
);

  assign ALUout3[3:0] = A ^ B;  // XOR_Gate xor_1, 4 bits wide
  assign ALUout3[7:4] = A | B;  // OR_Gate or_1, 4 bits wide
endmodule

module function4 (
  input  [3:0] A,
  input  [3:0] B,
  output [7:0] ALUout4
);

  wire or_1_out;

  assign ALUout4 = {{7{1'b0}}, or_1_out};  // Bit_Extender bit_extender_1
  or or_1 (or_1_out, A[0], A[1], A[2], A[3], B[0], B[1], B[2], B[3]);
endmodule

module function5 (
  input  [3:0] A,
  input  [3:0] B,
  output [7:0] AULout5
);


  assign AULout5 = {A, B};
endmodule

module lab3_part2 (
  input  SW8,
  input  [3:0] A_INPUT,
  input  [3:0] B_INPUT,
  output LEDR0,
  output LEDR1,
  output LEDR2,
  output LEDR4,
  output LEDR3
);

  wire FA1_cout, FA2_cout, FA3_cout;

  subcircuit FA1 (.A(A_INPUT[0]), .Cin(SW8), .B(B_INPUT[0]), .Cout(FA1_cout), .S(LEDR0));
  subcircuit FA2 (.A(A_INPUT[1]), .Cin(FA1_cout), .B(B_INPUT[1]), .Cout(FA2_cout), .S(LEDR1));
  subcircuit FA3 (.A(A_INPUT[2]), .Cin(FA2_cout), .B(B_INPUT[2]), .Cout(FA3_cout), .S(LEDR2));
  subcircuit FA4 (.A(A_INPUT[3]), .Cin(FA3_cout), .B(B_INPUT[3]), .Cout(LEDR4), .S(LEDR3));
endmodule

module display (
  input  c0,
  input  c1,
  input  c2,
  input  c3,
  output hex0,
  output hex1,
  output hex2,
  output hex3,
  output hex4,
  output hex5,
  output hex6
);

  hex_0 hex_0_1 (.c0(c0), .c1(c1), .c2(c2), .c3(c3), .hex0(hex0));
  hex_1 hex_1_1 (.c0(c0), .c1(c1), .c2(c2), .c3(c3), .hex1(hex1));
  hex_2 hex_2_1 (.c0(c0), .c1(c1), .c2(c2), .c3(c3), .hex2(hex2));
  hex_3 hex_3_1 (.c0(c0), .c1(c1), .c2(c2), .c3(c3), .hex3(hex3));
  hex_4 hex_4_1 (.c0(c0), .c1(c1), .c2(c2), .c3(c3), .hex4(hex4));
  hex_5 hex_5_1 (.c0(c0), .c1(c1), .c2(c2), .c3(c3), .hex5(hex5));
  hex_6 hex_6_1 (.c0(c0), .c1(c1), .c2(c2), .c3(c3), .hex6(hex6));
endmodule
