// Logisim project lab5_part3.circ as structural Verilog: 2 circuits, main circuit main
module main (
  input  SW_0,
  input  SW_1,
  input  SW_2,
  input  KEY1,
  input  KEY0
);

  wire Clk_out, ratedivider_1_out_out, undriven;
  wire [13:0] multiplexer_1_out;

  Clock Clk (.out(Clk_out));
  Multiplexer #(.enable("false"), .select(3), .width(14)) multiplexer_1 (
    .in0(14'h2a00), .in1(14'h3800), .in2(14'h2b80), .in3(14'h2ae0), .in4(14'h2ee0), .in5(14'h3ab8),
    .in6(14'h3aee), .in7(14'h3ba8), .out(multiplexer_1_out), .sel({SW_2, SW_1, SW_0}));
  RateDivider ratedivider_1 (.clear(KEY0), .clk(Clk_out), .out_out(ratedivider_1_out_out));
  // Shift_Register #(.length(14)) shift_register_1: pin names not known; wires that end beside it: KEY0, KEY1, 1'b1, ratedivider_1_out_out, 1'b0, multiplexer_1_out[0], multiplexer_1_out[1], multiplexer_1_out[2], multiplexer_1_out[3], multiplexer_1_out[4], multiplexer_1_out[5], multiplexer_1_out[6], multiplexer_1_out[7], multiplexer_1_out[8], multiplexer_1_out[9], multiplexer_1_out[10], multiplexer_1_out[11]
  LED LEDR0 (.in(undriven));
endmodule

module RateDivider (
  input  clear,
  input  clk,
  output out_out
);

  wire not_1_out, not_2_out, not_3_out;
  wire [2:0] counter_1_q;

  Counter #(.max('h7), .width(3)) counter_1 (
    .clr(clear), .load(out_out), .up(1'b0), .clk(clk), .D(3'b111), .Q(counter_1_q));  // open: count, carry
  not not_1 (not_1_out, counter_1_q[0]);
  not not_2 (not_2_out, counter_1_q[1]);
  not not_3 (not_3_out, counter_1_q[2]);
  and and_1 (out_out, not_1_out, not_2_out, not_3_out);
endmodule
