// Logisim project lab7_part1.circ as structural Verilog: 12 circuits, main circuit address_counter
module main (
  input  reset,
  input  WritenIn,
  output [4:0] out_3,
  output [3:0] out_4,
  output [3:0] out_5
);

  wire clk_out, display_1_hex0, display_1_hex1, display_1_hex2, display_1_hex3, display_1_hex4,
       display_1_hex5, display_1_hex6;

  Clock clk (.out(clk_out));
  address_counter address_counter_1 (.reset(reset), .clock(clk_out), .out_put(out_3));
  datain_counter datain_counter_1 (.reset(reset), .clock(clk_out), .out_put(out_5));
  ram_module ram_module_1 (.Address(out_3), .DataIn(out_5), .WritenIn(WritenIn), .Clock(clk_out), .Data_out(out_4));
  display display_1 (
    .c0(out_4[0]), .c1(out_4[1]), .c2(out_4[2]), .c3(out_4[3]), .hex0(display_1_hex0), .hex1(display_1_hex1),
    .hex2(display_1_hex2), .hex3(display_1_hex3), .hex4(display_1_hex4), .hex5(display_1_hex5),
    .hex6(display_1_hex6));
  _7_Segment_Display u_7_segment_display_1 (
    .g(display_1_hex6), .f(display_1_hex5), .a(display_1_hex0), .b(display_1_hex1), .e(display_1_hex4),
    .d(display_1_hex3), .c(display_1_hex2));  // open: dp
endmodule

module ram_module (
  input  [4:0] Address,
  input  [3:0] DataIn,
  input  WritenIn,
  input  Clock,
  output [3:0] Data_out
);

  wire not_1_out, register_3_q;
  wire [3:0] register_2_q;
  wire [4:0] register_1_q;

  Register #(.width(5)) register_1 (.D(Address), .en(1'b1), .clk(Clock), .Q(register_1_q));  // open: clr
  Register #(.width(4)) register_2 (.D(DataIn), .en(1'b1), .clk(Clock), .Q(register_2_q));  // open: clr
  Register #(.width(1)) register_3 (.D(WritenIn), .en(1'b1), .clk(Clock), .Q(register_3_q));  // open: clr
  not not_1 (not_1_out, register_3_q);
  RAM #(.addrWidth(5), .dataWidth(4)) ram_1 (
    .addr(register_1_q), .we(register_3_q), .oe(not_1_out), .clk(Clock), .din(register_2_q), .dout(Data_out));
endmodule

module address_counter (
  input  reset,
  input  clock,
  output [4:0] out_put
);

  Counter #(.max('h1f), .width(5)) counter_1 (
    .clr(reset), .load(1'b0), .up(1'b1), .clk(clock), .Q(out_put));  // open: count, D, carry
endmodule

module datain_counter (
  input  reset,
  input  clock,
  output [3:0] out_put
);

  wire and_1_out;

  Counter #(.max('hf), .width(4)) counter_1 (
    .clr(reset), .load(and_1_out), .up(1'b1), .clk(clock), .D(4'b0000), .Q(out_put));  // open: count, carry
  and and_1 (and_1_out, out_put[0], out_put[1], out_put[2], out_put[3]);
endmodule

module hex_0 (
  input  c0,
  input  c1,
  input  c2,
  input  c3,
  output hex0
);

  wire and_1_out, and_2_out, and_3_out, and_4_out, and_5_out, and_6_out, not_1_out, not_2_out, not_3_out,
       not_4_out;

  not not_1 (not_1_out, c0);
  not not_2 (not_2_out, c1);
  not not_3 (not_3_out, c2);
  not not_4 (not_4_out, c3);
  and and_1 (and_1_out, not_1_out, not_3_out);
  and and_2 (and_2_out, c1, not_4_out);
  and and_3 (and_3_out, not_4_out, c2, c0);
  and and_4 (and_4_out, c2, c1);
  and and_5 (and_5_out, c3, not_1_out);
  and and_6 (and_6_out, c3, not_2_out, not_3_out);
  or or_1 (hex0, and_1_out, and_2_out, and_3_out, and_4_out, and_5_out, and_6_out);

  // Notes on the sheet:
  //   HEX[0]
endmodule

module hex_1 (
  input  c0,
  input  c1,
  input  c2,
  input  c3,
  output hex1
);

  wire and_1_out, and_2_out, and_3_out, and_4_out, and_5_out, not_1_out, not_2_out, not_3_out, not_4_out;

  not not_1 (not_1_out, c0);
  not not_2 (not_2_out, c1);
  not not_3 (not_3_out, c2);
  not not_4 (not_4_out, c3);
  and and_1 (and_1_out, not_3_out, not_4_out);
  and and_2 (and_2_out, not_1_out, not_3_out);
  and and_3 (and_3_out, not_1_out, not_2_out, not_4_out);
  and and_4 (and_4_out, c0, not_2_out, c3);
  and and_5 (and_5_out, c0, c1, not_4_out);
  or or_1 (hex1, and_1_out, and_2_out, and_3_out, and_4_out, and_5_out);

  // Notes on the sheet:
  //   HEX[1]
endmodule

module hex_2 (
  input  c0,
  input  c1,
  input  c2,
  input  c3,
  output hex2
);

  wire and_1_out, and_2_out, and_3_out, and_4_out, and_5_out, not_1_out, not_2_out, not_3_out;

  not not_1 (not_1_out, c1);
  not not_2 (not_2_out, c2);
  not not_3 (not_3_out, c3);
  and and_1 (and_1_out, not_1_out, not_3_out);
  and and_2 (and_2_out, c0, not_3_out);
  and and_3 (and_3_out, not_1_out, c0);
  and and_4 (and_4_out, c2, not_3_out);
  and and_5 (and_5_out, not_2_out, c3);
  or or_1 (hex2, and_1_out, and_2_out, and_3_out, and_4_out, and_5_out);

  // Notes on the sheet:
  //   HEX[2]
endmodule

module hex_3 (
  input  c0,
  input  c1,
  input  c2,
  input  c3,
  output hex3
);

  wire and_1_out, and_2_out, and_3_out, and_4_out, and_5_out, not_1_out, not_2_out, not_3_out, not_4_out,
       not_5_out, not_6_out, not_7_out, not_8_out;

  not not_1 (not_1_out, c3);
  not not_2 (not_2_out, c1);
  not not_3 (not_3_out, c2);
  not not_4 (not_4_out, c0);
  not not_5 (not_5_out, c2);
  not not_6 (not_6_out, c0);
  not not_7 (not_7_out, c1);
  not not_8 (not_8_out, c0);
  and and_1 (and_1_out, not_1_out, not_3_out, not_4_out);
  and and_2 (and_2_out, not_5_out, c1, c0);
  and and_3 (and_3_out, c0, not_2_out, c2);
  and and_4 (and_4_out, not_6_out, not_7_out, c3);
  and and_5 (and_5_out, not_8_out, c1, c2);
  or or_1 (hex3, and_1_out, and_2_out, and_3_out, and_4_out, and_5_out);

  // Notes on the sheet:
  //   HEX[3]
endmodule

module hex_4 (
  input  c0,
  input  c1,
  input  c2,
  input  c3,
  output hex4
);

  wire and_1_out, and_2_out, and_3_out, and_4_out, not_1_out, not_2_out;

  not not_1 (not_1_out, c0);
  not not_2 (not_2_out, c2);
  and and_1 (and_1_out, not_1_out, not_2_out);
  and and_2 (and_2_out, not_1_out, c1);
  and and_3 (and_3_out, c2, c3);
  and and_4 (and_4_out, c1, c3);
  or or_1 (hex4, and_1_out, and_2_out, and_3_out, and_4_out);

  // Notes on the sheet:
  //   HEX[4]
endmodule

module hex_5 (
  input  c0,
  input  c1,
  input  c2,
  input  c3,
  output hex5
);

  wire and_1_out, and_2_out, and_3_out, and_4_out, and_5_out, not_1_out, not_2_out, not_3_out, not_4_out;

  not not_1 (not_1_out, c0);
  not not_2 (not_2_out, c1);
  not not_3 (not_3_out, c2);
  not not_4 (not_4_out, c3);
  and and_1 (and_1_out, not_1_out, not_2_out);
  and and_2 (and_2_out, not_1_out, c2);
  and and_3 (and_3_out, not_2_out, c2, not_4_out);
  and and_4 (and_4_out, not_3_out, c3);
  and and_5 (and_5_out, c1, c3);
  or or_1 (hex5, and_1_out, and_2_out, and_3_out, and_4_out, and_5_out);

  // Notes on the sheet:
  //   HEX[5]
endmodule

module hex_6 (
  input  c0,
  input  c1,
  input  c2,
  input  c3,
  output hex6
);

  wire and_1_out, and_2_out, and_3_out, and_4_out, and_5_out, not_1_out, not_2_out, not_3_out, not_4_out;

  not not_1 (not_1_out, c0);
  not not_2 (not_2_out, c1);
  not not_3 (not_3_out, c2);
  not not_4 (not_4_out, c3);
  and and_1 (and_1_out, not_3_out, c1);
  and and_2 (and_2_out, not_2_out, c2, not_4_out);
  and and_3 (and_3_out, c1, not_1_out);
  and and_4 (and_4_out, c3, c0);
  and and_5 (and_5_out, not_3_out, c3);
  or or_1 (hex6, and_1_out, and_2_out, and_3_out, and_4_out, and_5_out);

  // Notes on the sheet:
  //   HEX[6]
endmodule

module display (
  input  c0,
  input  c1,
  input  c2,
  input  c3,
  output hex0,
  output hex1,
  output hex2,
  output hex3,
  output hex4,
  output hex5,
  output hex6
);

  hex_0 hex_0_1 (.c0(c0), .c1(c1), .c2(c2), .c3(c3), .hex0(hex0));
  hex_1 hex_1_1 (.c0(c0), .c1(c1), .c2(c2), .c3(c3), .hex1(hex1));
  hex_2 hex_2_1 (.c0(c0), .c1(c1), .c2(c2), .c3(c3), .hex2(hex2));
  hex_3 hex_3_1 (.c0(c0), .c1(c1), .c2(c2), .c3(c3), .hex3(hex3));
  hex_4 hex_4_1 (.c0(c0), .c1(c1), .c2(c2), .c3(c3), .hex4(hex4));
  hex_5 hex_5_1 (.c0(c0), .c1(c1), .c2(c2), .c3(c3), .hex5(hex5));
  hex_6 hex_6_1 (.c0(c0), .c1(c1), .c2(c2), .c3(c3), .hex6(hex6));
endmodule
