// Logisim project lab7_part2.circ as structural Verilog: 3 circuits, main circuit main
module main (
  input  [6:0] X,
  input  [6:0] Y,
  input  reset,
  input  write_enable,
  input  [23:0] in_5
);

  wire clk_out;
  wire [6:0] data_path_1_xcoord, data_path_1_ycoord;
  wire [23:0] rgb_video_1_p6;

  Clock clk (.out(clk_out));
  data_path data_path_1 (
    .X(X), .reset(reset), .clk(clk_out), .Y(Y), .Xcoord(data_path_1_xcoord), .Ycoord(data_path_1_ycoord));
  // RGB_Video #(.cursor("No Cursor")) rgb_video_1: pin names not known; wires that end beside it: reset, clk_out, write_enable, data_path_1_xcoord, data_path_1_ycoord, rgb_video_1_p6
  colour colour_1 (.DateIn(in_5), .clk(clk_out), .out_put(rgb_video_1_p6));
endmodule

module colour (
  input  [23:0] DateIn,
  input  clk,
  output [23:0] out_put
);

  Register #(.width(24)) register_1 (.D(DateIn), .en(1'b1), .clk(clk), .Q(out_put));  // open: clr
endmodule

module data_path (
  input  [6:0] X,
  input  reset,
  input  clk,
  input  [6:0] Y,
  output [6:0] Xcoord,
  output [6:0] Ycoord
);

  wire and_1_out;
  wire [3:0] counter_1_q, counter_2_q;
  wire [6:0] bit_extender_1_out, bit_extender_2_out;

  Counter #(.max('hf), .width(4)) counter_1 (
    .clr(reset), .up(1'b1), .count(1'b1), .clk(clk), .D(4'b0000), .Q(counter_1_q));  // open: load, carry
  Counter #(.max('hf), .width(4)) counter_2 (
    .up(1'b1), .count(and_1_out), .clk(clk), .D(4'b0000), .Q(counter_2_q));  // open: clr, load, carry
  assign bit_extender_1_out = {{3{1'b0}}, counter_2_q};  // Bit_Extender bit_extender_1
  and and_1 (and_1_out, counter_1_q[0], counter_1_q[1], counter_1_q[2], counter_1_q[3]);
  Adder #(.width(7)) adder_1 (.a(bit_extender_1_out), .b(Y), .out(Ycoord));  // open: cin, cout
  assign bit_extender_2_out = {{3{1'b0}}, counter_1_q};  // Bit_Extender bit_extender_2
  Adder #(.width(7)) adder_2 (.a(bit_extender_2_out), .b(X), .out(Xcoord));  // open: cin, cout
endmodule
